# Fritzing sketch 2022 schematics (saved by Fritzing 0.9.6b)
breadboards: 1

parts:
  Garden_of_the_Day = Arduino Uno (Rev3)
  U1 = RELAY [package=relay-t9a]
  U2 = RELAY [package=relay-t9a]
  U3 = RELAY [package=relay-t9a]
  U4 = RELAY [package=relay-t9a]
  V1 = DC Power [voltage=5V]
  main = AC Power [voltage=220V frequency=60]
  Guardian_of_the_Night = Arduino Uno (Rev3)
  U5 = RELAY [package=relay-t9a]
  main1 = AC Power [voltage=220V frequency=60]
  V2 = DC Power [voltage=40V]
  main2 = AC Power [voltage=220V frequency=60]
  Part1 = IFR520 MOS module [package=THT]
  V3 = DC Power [voltage=12V]

nets:
  N1: Garden_of_the_Day.VIN, U5.NC
  N2: U1.MAIN, main.V+
  N3: U1.NO, Guardian_of_the_Night.VIN
  N4: U2.MAIN, V1.V+
  N5: U3.MAIN, V2.V+
  N6: U4.MAIN, main2.V+
  N7: Guardian_of_the_Night.D8, U5.COIL1
  N8: Guardian_of_the_Night.GND, U5.COIL2
  N9: U5.MAIN, main1.V-
  N10: Part1.VIN, V3.V+
